# Fritzing sketch arduino_sketch (saved by Fritzing 0.9.3b)
breadboards: 1

parts:
  U2 = NodeMCU V1.0
  Part1 = Adafruit TCS34725 RGB Color Sensor [part_number="Adafruit #1334"]
  LED = Header 3 [package=1x03-1mm-ra]
  12V/5V_DC-DC_Converter = Header 3 [package=1x03-1mm-ra]

nets:
  N1: U2.D1, Part1.SCL
  N2: U2.D2, Part1.SDA
  3V3: U2.3V3, Part1.+3V3
  GND: U2.GND, Part1.GND, Part1.LED_EN
  N3: U2.D5, LED.2
  N4: U2.RSV#40, 12V/5V_DC-DC_Converter.3
  GND_2: U2.RSV#41, LED.3, 12V/5V_DC-DC_Converter.2
  12V: LED.1, 12V/5V_DC-DC_Converter.1

notes:
  12V | Din | GND

custom parts:
  NodeMCU V1.0: ESP8266 based NodeMCU
  Adafruit TCS34725 RGB Color Sensor: Your electronics can now see in dazzling color with this lovely color light sensor. We found the best color sensor on the market, the TCS34725, which has RGB and Clear light sensing elements. An IR blocking filter, integrated on-chip and localized to the color sensing photodiodes, minimizes the IR spectral component of the incoming light and allows color measurements to be made accurately. The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
